# Fritzing sketch LoveCube (saved by Fritzing 0.9.4)
stripboards: 1

parts:
  U1 = ESP32S-HiLetgo [part_number=ESP32S-HiLetgo]

nets:
  N1: U1.3.3, U1.EN, U1.GPIO36, U1.GPIO39, U1.GPIO34, U1.GPIO35, U1.GPIO32, U1.GPIO33, U1.GPIO25, U1.GPIO26, U1.GPIO27, U1.GPIO14, U1.GPIO12, U1.GND, U1.GPIO13, U1.GPIO9, U1.GPIO10, U1.GPIO11, U1.GPIO7, U1.GPIO8, U1.GPIO15, U1.GPIO2, U1.GPIO0, U1.GPIO4, U1.GPIO16, U1.GPIO17, U1.GPIO5, U1.GPIO18, U1.GPIO19, U1.GPIO21, U1.GPIO3, U1.GPIO1, U1.GPIO22, U1.GPIO23

custom parts:
  ESP32S-HiLetgo: HiLetgo ESP-WROOM-32 ESP32 ESP-32S Development Board 2.4GHz Dual-Mode WiFi + Bluetooth Dual Cores Microcontroller The ESP32 integrated with Antenna switches, RF Balun, power amplifiers, low-noise amplifiers, filters, and management modules, and the entire solution occupies the least area of PCB. 2.4 GHz Wi-Fi plus Bluetooth dual-mode chip, with TSMC Ultra-low power consumption 40nm technology,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
